# Fritzing sketch fourServo (saved by Fritzing 0.9.0b)
breadboards: 5

parts:
  Part1 = Arduino Uno (Rev3)
  J1 = Basic Servo
  J2 = Basic Servo
  J3 = Basic Servo
  J4 = Basic Servo

nets:
  N1: Part1.D9_PWM, J3.pulse
  N2: Part1.D11_PWM/MOSI, J4.pulse
  N3: Part1.D3_PWM, J1.pulse
  N4: Part1.D6_PWM, J2.pulse
  GND: Part1.GND, J1.gnd, J2.gnd, J3.gnd, J4.gnd
  VCC: J1.vcc, J2.vcc, J3.vcc, J4.vcc
